# Fritzing sketch milestone2 (saved by Fritzing 0.9.3b)
circuit board: 6.88566cm x 5.36311cm
circuit board: 6.88566cm x 5.36311cm
breadboards: 1

parts:
  LCD_I2C = LCM1602 IIC [part_number="LCM1602 IIC" chip_label="LCM1602 IIC" package="DIP (Dual Inline) [THT]"]
  LCD = LCD-16X2 [package=lcd-16x2]
  Right_Eye = 1.2 Inch 8x8 LED Matrix Backpack [part_number=1052]
  Left_Eye = 1.2 Inch 8x8 LED Matrix Backpack [part_number=1052]
  Speaker = SPEAKER [package=pcb_mount_speaker]
  Right_Eyebrow = Basic Servo
  Tilt = Basic Servo
  Slave = Arduino Uno (Rev3)
  Master = Arduino Uno (Rev3)
  Pan = Basic Servo
  Left_Eyebrow = Basic Servo
  U1 = HC-SR04 [chip_label=IC package="SIP (Single Inline) [THT]"]
  VCC1 = Battery block 9V
  VCC2 = Battery block 9V
  S2 = Toggle Switch spst [package=THT]

nets:
  N1: LCD_I2C.VSS, LCD.K
  N2: LCD_I2C.VDD, LCD.A
  N3: LCD_I2C.V0, LCD.DB7
  N4: LCD_I2C.RS, LCD.DB6
  N5: LCD_I2C.RW, LCD.DB5
  N6: LCD_I2C.E, LCD.DB4
  N7: LCD_I2C.D0, LCD.DB3
  N8: LCD_I2C.D1, LCD.DB2
  N9: LCD_I2C.D2, LCD.DB1
  N10: LCD_I2C.D3, LCD.DB0
  N11: LCD_I2C.D4, LCD.E
  N12: LCD_I2C.D5, LCD.R_W
  N13: LCD_I2C.D6, LCD.RS
  N14: LCD_I2C.D7, LCD.VO
  N15: LCD_I2C.A, LCD.VDD
  N16: LCD_I2C.K, LCD.VSS
  GND: LCD_I2C.GND, Right_Eye.GND, Left_Eye.GND, Speaker.+, Right_Eyebrow.gnd, Tilt.gnd, Slave.GND, Master.GND, Pan.gnd, Left_Eyebrow.gnd, U1.GND, VCC1.-, VCC2.-
  VCC: LCD_I2C.VCC, Right_Eye.VDD, Left_Eye.VDD, Slave.VIN, Master.VIN, U1.Vcc, S2.COM
  N17: LCD_I2C.SDA, Right_Eye.SDA, Left_Eye.SDA, Slave.A4/SDA
  N18: LCD_I2C.SCL, Right_Eye.SCL, Left_Eye.SCL, Slave.A5/SCL
  N19: Speaker.-, Master.D5_PWM
  VCC_2: Right_Eyebrow.vcc, Tilt.vcc, Pan.vcc, Left_Eyebrow.vcc, VCC2.+
  N20: Right_Eyebrow.pulse, Master.D6_PWM
  N21: Tilt.pulse, Master.D8
  N22: Slave.A0, Master.A0
  N23: Master.A2, U1.Trig
  N24: Master.A3, U1.Echo
  N25: Master.D9_PWM, Pan.pulse
  N26: Master.D7, Left_Eyebrow.pulse

custom parts:
  LCM1602 IIC: I2C-Module to use a 1602 or 2004 LCD on with the wire.h libory Serial LCD Modul
  1.2 Inch 8x8 LED Matrix Backpack: This 1.2" 8x8 monochrome LED matrix includes a driver chip for simple control via an I2C interface. The backpack features address-selection jumpers so you can connect up to eight matrices on a single I2C bus.
  HC-SR04: HC-SR04 ultrasound distance sensor
  Toggle Switch spst: Toggle Switch single pole single throw
